// Logisim project processador.circ as structural Verilog: 4 circuits, main circuit main
module main (
  input  in_1,
  input  in_2,
  input  in_3,
  input  in_4,
  input  in_5,
  input  in_6,
  input  in_7,
  input  in_8,
  input  in_9,
  input  in_10,
  input  in_11,
  input  in_12,
  input  in_13,
  input  in_14,
  input  in_15,
  input  in_16,
  output [15:0] out_17
);

  wire clock_1_out, li_1_p2;
  wire [4:0] \pc_1_saída ;
  wire [15:0] demultiplexer_1_out0, demultiplexer_1_out1, demultiplexer_1_out2, demultiplexer_1_out3,
       demultiplexer_1_out4, demultiplexer_1_out5, register_1_q, register_2_q, register_3_q, register_4_q,
       register_5_q, register_6_q;

  PC pc_1 (.Clock(clock_1_out), .\Saída (\pc_1_saída ));
  Clock clock_1 (.out(clock_1_out));
  // li li_1: pin names not known; wires that end beside it: {in_4, in_5, in_6, in_7, in_8, in_9, in_10, in_11, in_12, in_13, in_14, in_15, in_16}, li_1_p2
  Decoder #(.select(3)) decoder_1 (
    .out1(li_1_p2), .sel({in_1, in_2, in_3}), .en(1'b1));  // open: out0, out2, out3, out4, out5, out6, out7
  RAM #(.addrWidth(5), .dataWidth(16), .bus("separate")) ram_1 (
    .addr(\pc_1_saída ), .data(out_17));  // open: din, str, sel, clk, ld, clr
  Demultiplexer #(.select(3), .width(16)) demultiplexer_1 (
    .out0(demultiplexer_1_out0), .out1(demultiplexer_1_out1), .out2(demultiplexer_1_out2),
    .out3(demultiplexer_1_out3), .out4(demultiplexer_1_out4), .out5(demultiplexer_1_out5));  // open: out6, out7, in, sel, en
  Register #(.width(16)) register_1 (.D(demultiplexer_1_out0), .Q(register_1_q));  // open: en, clk, clr
  Register #(.width(16)) register_2 (.D(demultiplexer_1_out1), .Q(register_2_q));  // open: en, clk, clr
  Register #(.width(16)) register_3 (.D(demultiplexer_1_out2), .Q(register_3_q));  // open: en, clk, clr
  Register #(.width(16)) register_4 (.D(demultiplexer_1_out3), .Q(register_4_q));  // open: en, clk, clr
  Register #(.width(16)) register_5 (.D(demultiplexer_1_out4), .Q(register_5_q));  // open: en, clk, clr
  Register #(.width(16)) register_6 (.D(demultiplexer_1_out5), .Q(register_6_q));  // open: en, clk, clr
  Multiplexer #(.select(3), .width(16)) multiplexer_1 (
    .in0(register_1_q), .in1(register_2_q), .in2(register_3_q), .in3(register_4_q), .in4(register_5_q),
    .in5(register_6_q));  // open: in6, in7, out, sel, en
  RAM ram_2 ();  // open: addr, data, sel, clk, ld, clr
endmodule

module decod_instr (
  input  in_1,
  input  in_2,
  input  in_3,
  input  in_4,
  input  in_5,
  input  in_6,
  input  in_7,
  input  in_8,
  input  in_9,
  input  in_10,
  input  in_11,
  input  in_12,
  input  in_13,
  input  in_14,
  input  in_15,
  input  in_16,
  output out_17
);

  Decoder #(.select(3)) decoder_1 (
    .out1(out_17), .sel({in_1, in_2, in_3}), .en(1'b1));  // open: out0, out2, out3, out4, out5, out6, out7
endmodule

module PC (
  input  Clock,
  output [4:0] \Saída 
);

  wire [4:0] adder_1_out;

  Register #(.width(5)) register_1 (.D(adder_1_out), .Q(\Saída ), .clk(Clock));  // open: en, clr
  Adder #(.width(5)) adder_1 (.a(5'b00001), .b(\Saída ), .out(adder_1_out));  // open: cin, cout
endmodule

module li (
  input  [12:0] \Instrução ,
  input  Ativo,
  output [15:0] Imediato,
  output [2:0] Reg_dest
);

  assign Imediato = {{6{1'b0}}, \Instrução [9:0]};  // Bit_Extender bit_extender_1

  assign Reg_dest = \Instrução [12:10];
endmodule
